# Fritzing sketch button (saved by Fritzing 0.7.4b)
breadboards: 1

parts:
  LED1 = LED - 3mm [color="Red (633nm)" package="3 mm [THT]"]
  R1 = Resistor [tolerance=±5% resistance=220 package=THT]
  Arduino1 = Arduino
  S1 = Pushbutton [package="[SMD]"]

nets:
  N1: LED1.cathode, Arduino1.D9
  N2: LED1.anode, R1.Pin_0
  N3: R1.Pin_1, Arduino1.GND, S1.Pin_3, S1.Pin_4
  N4: Arduino1.D2, S1.Pin_1, S1.Pin_2
