# Fritzing sketch light-sensor (saved by Fritzing 0.7.4b)
breadboards: 1

parts:
  LED1 = LED - 3mm [color="Red (633nm)" package="3 mm [THT]"]
  R1 = Resistor [tolerance=±5% resistance=220 package=THT]
  Arduino1 = Arduino
  R2 = Resistor [tolerance=±5% resistance=10k package=THT]
  R3 = Photocell (LDR) [package=THT]

nets:
  N1: LED1.cathode, Arduino1.D9
  N2: LED1.anode, R1.Pin_0
  N3: R1.Pin_1, Arduino1.GND, R3.pin_1
  N4: Arduino1.+5V, R2.Pin_1
  N5: Arduino1.A0, R2.Pin_0, R3.pin_0
