# Fritzing sketch pre-blink (saved by Fritzing 0.7.4b)
breadboards: 1

parts:
  LED1 = LED - 3mm [color="Red (633nm)" package="3 mm [THT]"]
  R1 = Resistor [tolerance=±5% resistance=220 package=THT]
  Arduino1 = Arduino

nets:
  N1: LED1.cathode, Arduino1.+5V
  N2: LED1.anode, R1.Pin_0
  N3: R1.Pin_1, Arduino1.GND
